// Logisim project parallel_to_UART.circ as structural Verilog: 3 circuits, main circuit main
module main (
);

  wire button_1_out, button_2_out, clock_1_out, parallel_to_uart_1_ready, parallel_to_uart_1_serial_out;
  wire [7:0] dipswitch_1_sw1;

  DipSwitch dipswitch_1 (
    .sw1(dipswitch_1_sw1[0]), .sw2(dipswitch_1_sw1[1]), .sw3(dipswitch_1_sw1[2]), .sw4(dipswitch_1_sw1[3]),
    .sw5(dipswitch_1_sw1[4]), .sw6(dipswitch_1_sw1[5]), .sw7(dipswitch_1_sw1[6]), .sw8(dipswitch_1_sw1[7]));
  Button button_1 (.out(button_1_out));
  Clock clock_1 (.out(clock_1_out));
  Button button_2 (.out(button_2_out));
  LED led_1 (.in(parallel_to_uart_1_ready));
  parallel_to_UART parallel_to_uart_1 (
    .clock(clock_1_out), .reset(button_2_out), .data_ready(button_1_out), .data(dipswitch_1_sw1),
    .ready(parallel_to_uart_1_ready), .serial_out(parallel_to_uart_1_serial_out));
  LED led_2 (.in(parallel_to_uart_1_serial_out));
endmodule

module parallel_to_UART (
  input  clock,
  input  reset,
  input  data_ready,
  input  [7:0] data,
  output ready,
  output serial_out
);

  wire done_sending, or_1_out, or_2_out, sr_latch_1_q;
  wire [3:0] bit_to_send;
  wire [7:0] register_1_q;

  or or_1 (or_1_out, done_sending, reset);
  SR_latch sr_latch_1 (.S(data_ready), .R(or_1_out), .Q(sr_latch_1_q));
  or or_2 (or_2_out, done_sending, reset);
  not not_1 (ready, sr_latch_1_q);
  Counter #(.max('hf), .width(4)) counter_1 (
    .clr(or_2_out), .load(1'b0), .up(1'b1), .count(sr_latch_1_q), .clk(clock), .Q(bit_to_send));  // open: D, carry
  Register register_1 (.D(data), .en(ready), .clk(data_ready), .Q(register_1_q), .clr(reset));
  Multiplexer #(.select(4)) multiplexer_1 (
    .in0(1'b1), .in1(1'b0), .in2(register_1_q[0]), .in3(register_1_q[1]), .in4(register_1_q[2]),
    .in5(register_1_q[3]), .in6(register_1_q[4]), .in7(register_1_q[5]), .in8(register_1_q[6]),
    .in9(register_1_q[7]), .in10(1'b1), .in11(1'b1), .out(serial_out), .sel(bit_to_send));  // open: in12, in13, in14, in15
  and and_1 (done_sending, bit_to_send[0], bit_to_send[1], ~bit_to_send[2], bit_to_send[3]);  // AND_Gate
endmodule

module SR_latch (
  input  S,
  input  R,
  output Q
);

  wire nor_2_out;

  nor nor_1 (Q, R, nor_2_out);
  nor nor_2 (nor_2_out, Q, S);
endmodule
